// Logisim project Mano Cpu Architecture.circ as structural Verilog: 40 circuits, main circuit main
module main (
  input  POWER,
  output [15:0] out_2,
  output [15:0] out_3,
  output [11:0] out_4,
  output [3:0] out_5,
  output [11:0] out_6,
  output [15:0] out_7,
  output [15:0] out_8,
  output [15:0] out_9,
  output [15:0] out_10
);

  wire ac_controller_1_add, ac_controller_1_andi, ac_controller_1_clr, ac_controller_1_comp,
       ac_controller_1_dr, ac_controller_1_inpr, ac_controller_1_inr, ac_controller_1_ld,
       ac_controller_1_shl, ac_controller_1_shr, and_1_out, ar_controller_1_clr, ar_controller_1_inr,
       ar_controller_1_ld, clk, dr_controller_1_inr, dr_controller_1_ld, E, E_OUT, FGI, FGO,
       flipflop_controller_1_e_reset, flipflop_controller_1_e_set, flipflop_controller_1_fgi_reset,
       flipflop_controller_1_fgo_reset, flipflop_controller_1_i_load, flipflop_controller_1_ien_reset,
       flipflop_controller_1_ien_set, flipflop_controller_1_r_reset, flipflop_controller_1_r_set,
       flipflop_controller_1_s_reset, flipflop_controller_1_sc_set, I, IEN, ir_controller_1_ld,
       mem_controller_1_read, mem_controller_1_write, not_1_out, not_2_out, not_3_out, not_4_out, not_5_out,
       or_1_out, outr_controller_1_ld, pc_controller_1_clr, pc_controller_1_inc, pc_controller_1_ld, R, S,
       SC, tr_controller_1_ld;
  wire [2:0] bus_controller_1_bus_select;
  wire [7:0] INPR_o;
  wire [15:0] alu_16_1_oupt, TR_o;

  reg8 INPR (.O(INPR_o));  // open: reset, set, load, I, clk
  and and_1 (and_1_out, clk, S);
  ALU_16 alu_16_1 (
    .ANDi(ac_controller_1_andi), .ADD(ac_controller_1_add), .DRi(ac_controller_1_dr),
    .INPRi(ac_controller_1_inpr), .COMP(ac_controller_1_comp), .SHR(ac_controller_1_shr),
    .SHL(ac_controller_1_shl), .AC(out_8), .DR(out_7), .INPR(INPR_o), .E_IN(E), .OUPT(alu_16_1_oupt),
    .E_out(E_OUT));
  AC_controller ac_controller_1 (
    .IR(out_9), .COUNTER(out_5), .INPR(ac_controller_1_inpr), .COMP(ac_controller_1_comp),
    .SHR(ac_controller_1_shr), .SHL(ac_controller_1_shl), .DR(ac_controller_1_dr), .ADD(ac_controller_1_add),
    .ANDi(ac_controller_1_andi), .LD(ac_controller_1_ld), .INR(ac_controller_1_inr), .CLR(ac_controller_1_clr));
  OUTR_controller outr_controller_1 (.IR(out_9), .COUNTER(out_5), .LD(outr_controller_1_ld));
  not not_1 (not_1_out, POWER);
  counter4 counter4_1 (.clear(SC), .load(not_1_out), .start(POWER), .Inpt(4'b0000), .clk(and_1_out), .out_6(out_5));
  reg8 OUTR (.load(outr_controller_1_ld), .I(out_3[7:0]), .clk(and_1_out));  // open: reset, set, O
  reg12 AR (
    .I(out_3[11:0]), .load(ar_controller_1_ld), .Inc(ar_controller_1_inr), .reset(ar_controller_1_clr),
    .clk(and_1_out), .O(out_4));
  reg12 PC (
    .I(out_3[11:0]), .load(pc_controller_1_ld), .Inc(pc_controller_1_inc), .reset(or_1_out), .clk(and_1_out),
    .O(out_6));
  not not_2 (not_2_out, POWER);
  reg16 DR (
    .I(out_3), .load(dr_controller_1_ld), .Inc(dr_controller_1_inr), .clk(and_1_out), .O(out_7));  // open: reset
  reg16 IR (.I(out_3), .load(ir_controller_1_ld), .clk(and_1_out), .O(out_9));  // open: Inc, reset
  reg16 TR (.I(out_3), .load(tr_controller_1_ld), .clk(and_1_out), .O(TR_o));  // open: Inc, reset
  FlipFlop_controller flipflop_controller_1 (
    .IEN(IEN), .FGI(FGI), .FGO(FGO), .R(R), .E(E_OUT), .AC(out_8), .IR(out_9), .COUNTER(out_5),
    .SC_set(flipflop_controller_1_sc_set), .S_reset(flipflop_controller_1_s_reset),
    .I_LOAD(flipflop_controller_1_i_load), .E_reset(flipflop_controller_1_e_reset),
    .E_set(flipflop_controller_1_e_set), .IEN_reset(flipflop_controller_1_ien_reset),
    .IEN_set(flipflop_controller_1_ien_set), .R_reset(flipflop_controller_1_r_reset),
    .FGO_reset(flipflop_controller_1_fgo_reset), .FGI_reset(flipflop_controller_1_fgi_reset),
    .R_set(flipflop_controller_1_r_set));
  or or_1 (or_1_out, not_2_out, pc_controller_1_clr);
  reg16 AC (
    .I(alu_16_1_oupt), .load(ac_controller_1_ld), .Inc(ac_controller_1_inr), .reset(ac_controller_1_clr),
    .clk(and_1_out), .O(out_8));
  mem_controller mem_controller_1 (
    .R(R), .IR(out_9), .COUNTER(out_5), .WRITE(mem_controller_1_write), .READ(mem_controller_1_read));
  not not_3 (not_3_out, flipflop_controller_1_s_reset);
  not not_4 (not_4_out, flipflop_controller_1_i_load);
  RAM #(.addrWidth(12), .asyncread("true"), .dataWidth(16)) ram_1 (
    .addr(out_4), .we(mem_controller_1_write), .oe(mem_controller_1_read), .clk(and_1_out), .din(out_3),
    .dout(out_2));
  PC_controller pc_controller_1 (
    .R(R), .E(E), .FGI(FGI), .FGO(FGO), .AC(out_8), .IR(out_9), .COUNTER(out_5), .INC(pc_controller_1_inc),
    .LD(pc_controller_1_ld), .CLR(pc_controller_1_clr));
  DR_controller dr_controller_1 (.IR(out_9), .COUNTER(out_5), .LD(dr_controller_1_ld), .INR(dr_controller_1_inr));
  IR_controller ir_controller_1 (.R(R), .COUNTER(out_5), .LD(ir_controller_1_ld));
  TR_controller tr_controller_1 (.R(R), .COUNTER(out_5), .LD(tr_controller_1_ld));
  not not_5 (not_5_out, flipflop_controller_1_sc_set);
  AR_controller ar_controller_1 (
    .R(R), .IR(out_9), .COUNTER(out_5), .CLR(ar_controller_1_clr), .LD(ar_controller_1_ld),
    .INR(ar_controller_1_inr));
  reg1 u_SC (.reset(not_5_out), .set(flipflop_controller_1_sc_set), .clk(and_1_out), .O(SC));
  reg1 u_S (.reset(flipflop_controller_1_s_reset), .set(not_3_out), .clk(and_1_out), .O(S));
  reg1 u_IEN (.reset(flipflop_controller_1_ien_reset), .set(flipflop_controller_1_ien_set), .clk(and_1_out), .O(IEN));
  reg1 u_I (.reset(not_4_out), .set(flipflop_controller_1_i_load), .clk(and_1_out), .O(I));
  reg1 u_R (.reset(flipflop_controller_1_r_reset), .set(flipflop_controller_1_r_set), .clk(and_1_out), .O(R));
  reg1 u_FGI (.reset(flipflop_controller_1_fgi_reset), .clk(and_1_out), .O(FGI));  // open: set
  reg1 u_FGO (.reset(flipflop_controller_1_fgo_reset), .clk(and_1_out), .O(FGO));  // open: set
  reg1 u_E (.reset(flipflop_controller_1_e_set), .set(flipflop_controller_1_e_reset), .clk(and_1_out), .O(E));
  Bus3to8 bus3to8_1 (
    .AR({4'b0000, out_4}), .PC({4'b0000, out_6}), .DR(out_7), .AC(out_8), .IR(out_9), .TR(TR_o), .MEM(out_2),
    .S2(bus_controller_1_bus_select[2]), .S1(bus_controller_1_bus_select[1]),
    .S0(bus_controller_1_bus_select[0]), .out_11(out_3));
  bus_controller bus_controller_1 (.R(R), .IR(out_9), .COUNTER(out_5), .BUS_SELECT(bus_controller_1_bus_select));
  Clock clock_1 (.out(clk));
  LED led_1 (.in(SC));
  LED led_2 (.in(S));
  LED led_3 (.in(IEN));
  LED led_4 (.in(I));
  LED led_5 (.in(R));
  LED led_6 (.in(FGI));
  LED led_7 (.in(FGO));
  LED led_8 (.in(E));

  // Other names for the same wires on the sheet: buss[15:0] = out_3; AR[11:0] = out_4; PC[11:0] = out_6;
  //   AC[15:0] = out_8; Counter[3:0] = out_5; DR[15:0] = out_7; IR[15:0] = out_9; MEM[15:0] = out_2;
  //   TR[15:0] = out_10
endmodule

module Bus3to8 (
  input  [15:0] AR,
  input  [15:0] PC,
  input  [15:0] DR,
  input  [15:0] AC,
  input  [15:0] IR,
  input  [15:0] TR,
  input  S2,
  input  S1,
  input  S0,
  input  [15:0] MEM,
  output [15:0] out_11
);

  Multiplexer #(.select(3), .width(16)) multiplexer_1 (
    .in0({16{1'b0}}), .in1(AR), .in2(PC), .in3(DR), .in4(AC), .in5(IR), .in6(TR), .in7(MEM), .out(out_11),
    .sel({S2, S1, S0}));
endmodule

module bus_controller (
  input  R,
  input  [15:0] IR,
  input  [3:0] COUNTER,
  output [2:0] BUS_SELECT
);

  wire and_1_out, and_2_out, and_5_out, and_6_out, and_7_out, and_8_out, and_9_out, and_10_out, and_11_out,
       and_12_out, and_13_out, and_14_out, and_15_out, and_16_out, and_17_out, BUS1, BUS2, BUS3, BUS4, BUS5,
       BUS6, BUS7, D0, D1, D2, D3, D4, D5, D6, D7, not_1_out, not_2_out, not_3_out, not_4_out, not_5_out, p,
       r_t, T0, T1, T2, T3, T4, T5, T6, T7, T8, T9, T10, T11, T12, T13, T14, T15;

  Decoder4to16 decoder4to16_1 (
    .I0(COUNTER[0]), .I1(COUNTER[1]), .I2(COUNTER[2]), .I3(COUNTER[3]), .O1(T0), .O2(T1), .O3(T2), .O4(T3),
    .O5(T4), .O6(T5), .O7(T6), .O8(T7), .O9(T8), .O10(T9), .O11(T10), .O12(T11), .O13(T12), .O14(T13),
    .O15(T14), .O16(T15));
  and and_1 (and_1_out, D4, T4);
  and and_2 (and_2_out, D5, T5);
  or or_1 (BUS1, and_1_out, and_2_out);
  and and_3 (p, D7, IR[15], T3);
  Priority_Encoder priority_encoder_1 (
    .in0(1'b0), .in1(BUS1), .in2(BUS2), .in3(BUS3), .in4(BUS4), .in5(BUS5), .in6(BUS6), .in7(BUS7),
    .out(BUS_SELECT));  // open: en_in, gs, en_out
  not not_1 (not_1_out, IR[15]);
  Decoder3to8 decoder3to8_1 (
    .I0(IR[12]), .I1(IR[13]), .I2(IR[14]), .O0(D0), .O1(D1), .O2(D2), .O3(D3), .out_8(D4), .out_9(D5),
    .out_10(D6), .out_11(D7));
  not not_2 (not_2_out, R);
  and and_4 (r_t, D7, not_1_out, T3);
  and and_5 (and_5_out, not_2_out, T0);
  and and_6 (and_6_out, R, T0);
  and and_7 (and_7_out, D5, T4);
  or or_2 (BUS2, and_5_out, and_6_out, and_7_out);
  and and_8 (and_8_out, D2, T5);
  and and_9 (and_9_out, D6, T6);
  not not_3 (not_3_out, R);
  and and_10 (and_10_out, not_3_out, T1);
  and and_11 (and_11_out, D0, T4);
  and and_12 (and_12_out, D1, T4);
  and and_13 (and_13_out, D2, T4);
  and and_14 (and_14_out, D6, T4);
  or or_3 (BUS3, and_8_out, and_9_out);
  or or_4 (BUS7, and_10_out, and_11_out, and_12_out, and_13_out, and_14_out, and_15_out);
  not not_4 (not_4_out, D7);
  and and_15 (and_15_out, not_4_out, IR[15], T3);
  and and_16 (and_16_out, D3, T4);
  and and_17 (and_17_out, p, IR[10]);
  not not_5 (not_5_out, R);
  or or_5 (BUS4, and_16_out, and_17_out);
  and and_18 (BUS5, not_5_out, T2);
  and and_19 (BUS6, R, T1);

  // Other names for the same wires on the sheet: B0 = IR[0]; B1 = IR[1]; B2 = IR[2]; B3 = IR[3]; B4 = IR[4];
  //   B5 = IR[5]; B6 = IR[6]; B7 = IR[7]; B8 = IR[8]; B9 = IR[9]; B10 = IR[10]; B11 = IR[11]; I = IR[15]
endmodule

module Decoder3to8 (
  input  I0,
  input  I1,
  input  I2,
  output O0,
  output O1,
  output O2,
  output O3,
  output out_8,
  output out_9,
  output out_10,
  output out_11
);

  wire not_1_out, not_2_out, not_3_out;

  not not_1 (not_1_out, I2);
  not not_2 (not_2_out, I1);
  not not_3 (not_3_out, I0);
  and and_1 (O0, not_3_out, not_1_out, not_2_out);
  and and_2 (O1, I0, not_2_out, not_1_out);
  and and_3 (O2, not_3_out, I1, not_1_out);
  and and_4 (O3, I0, I1, not_1_out);
  and and_5 (out_8, not_3_out, not_2_out, I2);
  and and_6 (out_9, I0, not_2_out, I2);
  and and_7 (out_10, not_3_out, I1, I2);
  and and_8 (out_11, I0, I1, I2);
endmodule

module Decoder4to16 (
  input  I0,
  input  I1,
  input  I2,
  input  I3,
  output O1,
  output O2,
  output O3,
  output O4,
  output O5,
  output O6,
  output O7,
  output O8,
  output O9,
  output O10,
  output O11,
  output O12,
  output O13,
  output O14,
  output O15,
  output O16
);

  wire decoder2to4_1_o0, decoder2to4_1_o1, decoder2to4_1_o2, decoder2to4_1_o3;

  Decoder2to4 decoder2to4_1 (
    .I1(I3), .I0(I2), .enable(1'b1), .O0(decoder2to4_1_o0), .O1(decoder2to4_1_o1), .O2(decoder2to4_1_o2),
    .O3(decoder2to4_1_o3));
  Decoder2to4 decoder2to4_2 (.I1(I1), .I0(I0), .enable(decoder2to4_1_o0), .O0(O1), .O1(O2), .O2(O3), .O3(O4));
  Decoder2to4 decoder2to4_3 (.I1(I1), .I0(I0), .enable(decoder2to4_1_o1), .O0(O5), .O1(O6), .O2(O7), .O3(O8));
  Decoder2to4 decoder2to4_4 (.I1(I1), .I0(I0), .enable(decoder2to4_1_o2), .O0(O9), .O1(O10), .O2(O11), .O3(O12));
  Decoder2to4 decoder2to4_5 (.I1(I1), .I0(I0), .enable(decoder2to4_1_o3), .O0(O13), .O1(O14), .O2(O15), .O3(O16));
endmodule

module Decoder2to4 (
  input  I1,
  input  I0,
  input  enable,
  output O0,
  output O1,
  output O2,
  output O3
);

  wire not_1_out, not_2_out;

  not not_1 (not_1_out, I0);
  not not_2 (not_2_out, I1);
  and and_1 (O0, not_2_out, enable, not_1_out);
  and and_2 (O1, not_2_out, enable, I0);
  and and_3 (O2, I1, enable, not_1_out);
  and and_4 (O3, I1, enable, I0);
endmodule

module Reg1bit (
  input  set,
  input  reset,
  input  clk,
  input  I,
  output O
);

  D_Flip_Flop d_ff_1 (.D(I), .clk(clk), .Q(O), .preset(set), .reset(reset));  // open: Qn
endmodule

module Reg8bit (
  input  set,
  input  reset,
  input  clk,
  input  [7:0] I,
  output [7:0] O
);

  D_Flip_Flop d_ff_1 (.D(I[0]), .clk(clk), .Q(O[0]), .preset(set), .reset(reset));  // open: Qn
  D_Flip_Flop d_ff_2 (.D(I[1]), .clk(clk), .Q(O[1]), .preset(set), .reset(reset));  // open: Qn
  D_Flip_Flop d_ff_3 (.D(I[2]), .clk(clk), .Q(O[2]), .preset(set), .reset(reset));  // open: Qn
  D_Flip_Flop d_ff_4 (.D(I[3]), .clk(clk), .Q(O[3]), .preset(set), .reset(reset));  // open: Qn
  D_Flip_Flop d_ff_5 (.D(I[4]), .clk(clk), .Q(O[4]), .preset(set), .reset(reset));  // open: Qn
  D_Flip_Flop d_ff_6 (.D(I[5]), .clk(clk), .Q(O[5]), .preset(set), .reset(reset));  // open: Qn
  D_Flip_Flop d_ff_7 (.D(I[6]), .clk(clk), .Q(O[6]), .preset(set), .reset(reset));  // open: Qn
  D_Flip_Flop d_ff_8 (.D(I[7]), .clk(clk), .Q(O[7]), .preset(set), .reset(reset));  // open: Qn
endmodule

module Reg12bit (
  input  set,
  input  reset,
  input  clk,
  input  [11:0] I,
  output [11:0] out_5
);

  D_Flip_Flop d_ff_1 (.D(I[0]), .clk(clk), .Q(out_5[0]), .preset(set), .reset(reset));  // open: Qn
  D_Flip_Flop d_ff_2 (.D(I[1]), .clk(clk), .Q(out_5[1]), .preset(set), .reset(reset));  // open: Qn
  D_Flip_Flop d_ff_3 (.D(I[2]), .clk(clk), .Q(out_5[2]), .preset(set), .reset(reset));  // open: Qn
  D_Flip_Flop d_ff_4 (.D(I[3]), .clk(clk), .Q(out_5[3]), .preset(set), .reset(reset));  // open: Qn
  D_Flip_Flop d_ff_5 (.D(I[4]), .clk(clk), .Q(out_5[4]), .preset(set), .reset(reset));  // open: Qn
  D_Flip_Flop d_ff_6 (.D(I[5]), .clk(clk), .Q(out_5[5]), .preset(set), .reset(reset));  // open: Qn
  D_Flip_Flop d_ff_7 (.D(I[6]), .clk(clk), .Q(out_5[6]), .preset(set), .reset(reset));  // open: Qn
  D_Flip_Flop d_ff_8 (.D(I[7]), .clk(clk), .Q(out_5[7]), .preset(set), .reset(reset));  // open: Qn
  D_Flip_Flop d_ff_9 (.D(I[8]), .clk(clk), .Q(out_5[8]), .preset(set), .reset(reset));  // open: Qn
  D_Flip_Flop d_ff_10 (.D(I[9]), .clk(clk), .Q(out_5[9]), .preset(set), .reset(reset));  // open: Qn
  D_Flip_Flop d_ff_11 (.D(I[10]), .clk(clk), .Q(out_5[10]), .preset(set), .reset(reset));  // open: Qn
  D_Flip_Flop d_ff_12 (.D(I[11]), .clk(clk), .Q(out_5[11]), .preset(set), .reset(reset));  // open: Qn
endmodule

module Reg16bit (
  input  set,
  input  reset,
  input  clk,
  input  [15:0] I,
  output [15:0] out_5
);

  D_Flip_Flop d_ff_1 (.D(I[0]), .clk(clk), .Q(out_5[0]), .preset(set), .reset(reset));  // open: Qn
  D_Flip_Flop d_ff_2 (.D(I[1]), .clk(clk), .Q(out_5[1]), .preset(set), .reset(reset));  // open: Qn
  D_Flip_Flop d_ff_3 (.D(I[2]), .clk(clk), .Q(out_5[2]), .preset(set), .reset(reset));  // open: Qn
  D_Flip_Flop d_ff_4 (.D(I[3]), .clk(clk), .Q(out_5[3]), .preset(set), .reset(reset));  // open: Qn
  D_Flip_Flop d_ff_5 (.D(I[4]), .clk(clk), .Q(out_5[4]), .preset(set), .reset(reset));  // open: Qn
  D_Flip_Flop d_ff_6 (.D(I[5]), .clk(clk), .Q(out_5[5]), .preset(set), .reset(reset));  // open: Qn
  D_Flip_Flop d_ff_7 (.D(I[6]), .clk(clk), .Q(out_5[6]), .preset(set), .reset(reset));  // open: Qn
  D_Flip_Flop d_ff_8 (.D(I[7]), .clk(clk), .Q(out_5[7]), .preset(set), .reset(reset));  // open: Qn
  D_Flip_Flop d_ff_9 (.D(I[8]), .clk(clk), .Q(out_5[8]), .preset(set), .reset(reset));  // open: Qn
  D_Flip_Flop d_ff_10 (.D(I[9]), .clk(clk), .Q(out_5[9]), .preset(set), .reset(reset));  // open: Qn
  D_Flip_Flop d_ff_11 (.D(I[10]), .clk(clk), .Q(out_5[10]), .preset(set), .reset(reset));  // open: Qn
  D_Flip_Flop d_ff_12 (.D(I[11]), .clk(clk), .Q(out_5[11]), .preset(set), .reset(reset));  // open: Qn
  D_Flip_Flop d_ff_13 (.D(I[12]), .clk(clk), .Q(out_5[12]), .preset(set), .reset(reset));  // open: Qn
  D_Flip_Flop d_ff_14 (.D(I[13]), .clk(clk), .Q(out_5[13]), .preset(set), .reset(reset));  // open: Qn
  D_Flip_Flop d_ff_15 (.D(I[14]), .clk(clk), .Q(out_5[14]), .preset(set), .reset(reset));  // open: Qn
  D_Flip_Flop d_ff_16 (.D(I[15]), .clk(clk), .Q(out_5[15]), .preset(set), .reset(reset));  // open: Qn
endmodule

module mux_r1 (
  input  A,
  input  I1,
  input  I2,
  output O
);

  wire and_1_out, and_2_out, not_1_out;

  not not_1 (not_1_out, A);
  and and_1 (and_1_out, not_1_out, I1);
  and and_2 (and_2_out, A, I2);
  or or_1 (O, and_1_out, and_2_out);
endmodule

module mux_r8 (
  input  A,
  input  [7:0] I1,
  input  [7:0] I2,
  output [7:0] O
);

  wire [7:0] and_1_out, and_2_out, not_1_out;

  assign not_1_out = ~{8{A}};  // NOT_Gate not_1, 8 bits wide
  assign and_1_out = not_1_out & I1;  // AND_Gate and_1, 8 bits wide
  assign and_2_out = {8{A}} & I2;  // AND_Gate and_2, 8 bits wide
  assign O = and_1_out | and_2_out;  // OR_Gate or_1, 8 bits wide
endmodule

module mux_r12 (
  input  A,
  input  [11:0] I1,
  input  [11:0] I2,
  output [11:0] O
);

  wire [11:0] and_1_out, and_2_out, not_1_out;

  assign not_1_out = ~{12{A}};  // NOT_Gate not_1, 12 bits wide
  assign and_1_out = not_1_out & I1;  // AND_Gate and_1, 12 bits wide
  assign and_2_out = {12{A}} & I2;  // AND_Gate and_2, 12 bits wide
  assign O = and_1_out | and_2_out;  // OR_Gate or_1, 12 bits wide
endmodule

module mux_r16 (
  input  A,
  input  [15:0] I1,
  input  [15:0] I2,
  output [15:0] O
);

  wire [15:0] and_1_out, and_2_out, not_1_out;

  assign not_1_out = ~{16{A}};  // NOT_Gate not_1, 16 bits wide
  assign and_1_out = not_1_out & I1;  // AND_Gate and_1, 16 bits wide
  assign and_2_out = {16{A}} & I2;  // AND_Gate and_2, 16 bits wide
  assign O = and_1_out | and_2_out;  // OR_Gate or_1, 16 bits wide
endmodule

module reg1 (
  input  reset,
  input  set,
  input  clk,
  output O
);

  Reg1bit reg1bit_1 (.set(set), .reset(reset), .clk(clk), .I(O), .O(O));
endmodule

module reg8 (
  input  reset,
  input  set,
  input  load,
  input  [7:0] I,
  input  clk,
  output [7:0] O
);

  wire [7:0] mux_r8_1_o;

  mux_r8 mux_r8_1 (.A(load), .I1(O), .I2(I), .O(mux_r8_1_o));
  Reg8bit reg8bit_1 (.set(set), .reset(reset), .clk(clk), .I(mux_r8_1_o), .O(O));
endmodule

module reg12 (
  input  reset,
  input  load,
  input  [11:0] I,
  input  clk,
  input  Inc,
  output [11:0] O
);

  wire [11:0] adder16bit_1_sum, mux_r12_1_o, mux_r12_2_o;
  wire [15:0] undriven;
  wire [15:12] adder16bit_1_sum_2;

  Adder16bit adder16bit_1 (
    .A({4'b0000, O}), .B(undriven), .caryyIn(1'b1), .sum({adder16bit_1_sum_2, adder16bit_1_sum}));  // open: carry
  mux_r12 mux_r12_1 (.A(load), .I1(mux_r12_2_o), .I2(I), .O(mux_r12_1_o));
  mux_r12 mux_r12_2 (.A(Inc), .I1(O), .I2(adder16bit_1_sum), .O(mux_r12_2_o));
  Reg12bit reg12bit_1 (.set(1'b0), .reset(reset), .clk(clk), .I(mux_r12_1_o), .out_5(O));
endmodule

module reg16 (
  input  reset,
  input  load,
  input  [15:0] I,
  input  clk,
  input  Inc,
  output [15:0] O
);

  wire [15:0] adder16bit_1_sum, mux_r16_1_o, mux_r16_2_o;

  Adder16bit adder16bit_1 (.A(O), .caryyIn(1'b1), .sum(adder16bit_1_sum));  // open: B, carry
  mux_r16 mux_r16_1 (.A(load), .I1(mux_r16_2_o), .I2(I), .O(mux_r16_1_o));
  mux_r16 mux_r16_2 (.A(Inc), .I1(O), .I2(adder16bit_1_sum), .O(mux_r16_2_o));
  Reg16bit reg16bit_1 (.set(1'b0), .reset(reset), .clk(clk), .I(mux_r16_1_o), .out_5(O));
endmodule

module Adder1bit (
  input  A,
  input  B,
  input  Cin,
  output Sum,
  output Carry
);

  wire and_1_out, and_2_out, xor_1_out;

  and and_1 (and_1_out, B, A);
  xor xor_1 (xor_1_out, A, B);
  xor xor_2 (Sum, xor_1_out, Cin);
  and and_2 (and_2_out, xor_1_out, Cin);
  or or_1 (Carry, and_2_out, and_1_out);
endmodule

module Adder2bit (
  input  A1,
  input  B1,
  input  C,
  input  A2,
  input  B2,
  output S1,
  output S2,
  output Carry
);

  wire adder1bit_1_carry;

  Adder1bit adder1bit_1 (.A(A1), .B(B1), .Cin(C), .Sum(S1), .Carry(adder1bit_1_carry));
  Adder1bit adder1bit_2 (.A(A2), .B(B2), .Cin(adder1bit_1_carry), .Sum(S2), .Carry(Carry));
endmodule

module Adder4bit (
  input  A1,
  input  B1,
  input  C,
  input  A2,
  input  B2,
  input  A3,
  input  B3,
  input  A4,
  input  B4,
  output S1,
  output S2,
  output S3,
  output S4,
  output Carry
);

  wire adder2bit_1_carry;

  Adder2bit adder2bit_1 (.A1(A1), .B1(B1), .C(C), .A2(A2), .B2(B2), .S1(S1), .S2(S2), .Carry(adder2bit_1_carry));
  Adder2bit adder2bit_2 (.A1(A3), .B1(B3), .C(adder2bit_1_carry), .A2(A4), .B2(B4), .S1(S3), .S2(S4), .Carry(Carry));
endmodule

module Adder8bit (
  input  A1,
  input  A2,
  input  A3,
  input  A4,
  input  A5,
  input  A6,
  input  A7,
  input  A8,
  input  B1,
  input  B2,
  input  B3,
  input  B4,
  input  B5,
  input  B6,
  input  B7,
  input  B8,
  input  C,
  output S1,
  output S2,
  output S3,
  output S4,
  output S5,
  output S6,
  output S7,
  output S8,
  output Carry
);

  wire adder4bit_1_carry;

  Adder4bit adder4bit_1 (
    .A1(A1), .B1(B1), .C(C), .A2(A2), .B2(B2), .A3(A3), .B3(B3), .A4(A4), .B4(B4), .S1(S1), .S2(S2), .S3(S3),
    .S4(S4), .Carry(adder4bit_1_carry));
  Adder4bit adder4bit_2 (
    .A1(A5), .B1(B5), .C(adder4bit_1_carry), .A2(A6), .B2(B6), .A3(A7), .B3(B7), .A4(A8), .B4(B8), .S1(S5),
    .S2(S6), .S3(S7), .S4(S8), .Carry(Carry));
endmodule

module Adder16bit (
  input  [15:0] A,
  input  [15:0] B,
  input  caryyIn,
  output [15:0] sum,
  output carry
);

  wire adder8bit_1_carry;

  Adder8bit adder8bit_1 (
    .A1(A[0]), .A2(A[1]), .A3(A[2]), .A4(A[3]), .A5(A[4]), .A6(A[5]), .A7(A[6]), .A8(A[7]), .B1(B[0]),
    .B2(B[1]), .B3(B[2]), .B4(B[3]), .B5(B[4]), .B6(B[5]), .B7(B[6]), .B8(B[7]), .C(caryyIn), .S1(sum[0]),
    .S2(sum[1]), .S3(sum[2]), .S4(sum[3]), .S5(sum[4]), .S6(sum[5]), .S7(sum[6]), .S8(sum[7]),
    .Carry(adder8bit_1_carry));
  Adder8bit adder8bit_2 (
    .A1(A[8]), .A2(A[9]), .A3(A[10]), .A4(A[11]), .A5(A[12]), .A6(A[13]), .A7(A[14]), .A8(A[15]), .B1(B[8]),
    .B2(B[9]), .B3(B[10]), .B4(B[11]), .B5(B[12]), .B6(B[13]), .B7(B[14]), .B8(B[15]), .C(adder8bit_1_carry),
    .S1(sum[8]), .S2(sum[9]), .S3(sum[10]), .S4(sum[11]), .S5(sum[12]), .S6(sum[13]), .S7(sum[14]),
    .S8(sum[15]), .Carry(carry));
endmodule

module counter4 (
  input  clear,
  input  load,
  input  start,
  input  [3:0] Inpt,
  input  clk,
  output [3:0] out_6
);

  wire and_1_out, and_2_out, and_3_out, and_4_out, and_5_out, and_6_out, and_7_out, and_8_out, and_9_out,
       and_10_out, and_11_out, and_12_out, and_13_out, and_14_out, not_1_out, not_2_out, not_3_out,
       not_4_out, not_5_out, not_6_out, or_1_out, or_2_out, or_3_out, or_4_out, or_5_out, or_6_out, or_7_out,
       or_8_out;

  not not_1 (not_1_out, clear);
  not not_2 (not_2_out, load);
  and and_1 (and_1_out, not_1_out, load);
  not not_3 (not_3_out, Inpt[0]);
  not not_4 (not_4_out, Inpt[1]);
  not not_5 (not_5_out, Inpt[2]);
  not not_6 (not_6_out, Inpt[3]);
  and and_2 (and_2_out, and_1_out, Inpt[0]);
  and and_3 (and_3_out, not_3_out, and_1_out);
  and and_4 (and_4_out, and_1_out, Inpt[1]);
  and and_5 (and_5_out, not_4_out, and_1_out);
  and and_6 (and_6_out, and_1_out, Inpt[2]);
  and and_7 (and_7_out, not_5_out, and_1_out);
  and and_8 (and_8_out, and_1_out, Inpt[3]);
  and and_9 (and_9_out, not_6_out, and_1_out);
  and and_10 (and_10_out, not_1_out, not_2_out, start);
  and and_11 (and_11_out, and_10_out, out_6[0]);
  and and_12 (and_12_out, and_11_out, out_6[1]);
  and and_13 (and_13_out, and_12_out, out_6[2]);
  and and_14 (and_14_out, and_13_out, out_6[3]);
  J_K_Flip_Flop j_k_ff_1 (.J(or_1_out), .K(or_2_out), .clk(clk), .Q(out_6[0]));  // open: Qn, preset, reset
  or or_1 (or_1_out, and_10_out, and_2_out);
  or or_2 (or_2_out, clear, and_10_out, and_3_out);
  J_K_Flip_Flop j_k_ff_2 (.J(or_3_out), .K(or_4_out), .clk(clk), .Q(out_6[1]));  // open: Qn, preset, reset
  or or_3 (or_3_out, and_11_out, and_4_out);
  or or_4 (or_4_out, clear, and_11_out, and_5_out);
  J_K_Flip_Flop j_k_ff_3 (.J(or_5_out), .K(or_6_out), .clk(clk), .Q(out_6[2]));  // open: Qn, preset, reset
  or or_5 (or_5_out, and_12_out, and_6_out);
  or or_6 (or_6_out, clear, and_12_out, and_7_out);
  J_K_Flip_Flop j_k_ff_4 (.J(or_7_out), .K(or_8_out), .clk(clk), .Q(out_6[3]));  // open: Qn, preset, reset
  or or_7 (or_7_out, and_13_out, and_8_out);
  or or_8 (or_8_out, clear, and_13_out, and_9_out);
endmodule

module AR_controller (
  input  R,
  input  [15:0] IR,
  input  [3:0] COUNTER,
  output LD,
  output CLR,
  output INR
);

  wire and_3_out, and_4_out, and_5_out, D0, D1, D2, D3, D4, D5, D6, D7, not_1_out, not_2_out, not_3_out, p,
       r_t, T0, T1, T2, T3, T4, T5, T6, T7, T8, T9, T10, T11, T12, T13, T14, T15;

  Decoder4to16 decoder4to16_1 (
    .I0(COUNTER[0]), .I1(COUNTER[1]), .I2(COUNTER[2]), .I3(COUNTER[3]), .O1(T0), .O2(T1), .O3(T2), .O4(T3),
    .O5(T4), .O6(T5), .O7(T6), .O8(T7), .O9(T8), .O10(T9), .O11(T10), .O12(T11), .O13(T12), .O14(T13),
    .O15(T14), .O16(T15));
  and and_1 (p, D7, IR[15], T3);
  not not_1 (not_1_out, IR[15]);
  Decoder3to8 decoder3to8_1 (
    .I0(IR[12]), .I1(IR[13]), .I2(IR[14]), .O0(D0), .O1(D1), .O2(D2), .O3(D3), .out_8(D4), .out_9(D5),
    .out_10(D6), .out_11(D7));
  not not_2 (not_2_out, R);
  not not_3 (not_3_out, D7);
  and and_2 (r_t, D7, not_1_out, T3);
  and and_3 (and_3_out, not_2_out, T0);
  and and_4 (and_4_out, not_2_out, T2);
  and and_5 (and_5_out, not_3_out, IR[15], T3);
  or or_1 (LD, and_3_out, and_4_out, and_5_out);
  and and_6 (INR, D5, T4);
  and and_7 (CLR, R, T0);

  // Other names for the same wires on the sheet: B0 = IR[0]; B1 = IR[1]; B2 = IR[2]; B3 = IR[3]; B4 = IR[4];
  //   B5 = IR[5]; B6 = IR[6]; B7 = IR[7]; B8 = IR[8]; B9 = IR[9]; B10 = IR[10]; B11 = IR[11]; I = IR[15]
endmodule

module PC_controller (
  input  [15:0] AC,
  input  R,
  input  E,
  input  FGI,
  input  [15:0] IR,
  input  FGO,
  input  [3:0] COUNTER,
  output LD,
  output CLR,
  output INC
);

  wire AC_t, and_3_out, and_4_out, and_6_out, and_7_out, and_8_out, and_9_out, and_10_out, and_11_out,
       and_12_out, and_13_out, and_14_out, D0, D1, D2, D3, D4, D5, D6, D7, not_1_out, not_2_out, not_3_out,
       not_4_out, not_5_out, p, r_t, T0, T1, T2, T3, T4, T5, T6, T7, T8, T9, T10, T11, T12, T13, T14, T15;

  Decoder4to16 decoder4to16_1 (
    .I0(COUNTER[0]), .I1(COUNTER[1]), .I2(COUNTER[2]), .I3(COUNTER[3]), .O1(T0), .O2(T1), .O3(T2), .O4(T3),
    .O5(T4), .O6(T5), .O7(T6), .O8(T7), .O9(T8), .O10(T9), .O11(T10), .O12(T11), .O13(T12), .O14(T13),
    .O15(T14), .O16(T15));
  or or_1 (AC_t, AC[0], AC[1], AC[2], AC[3], AC[4], AC[5], AC[6], AC[7], AC[8], AC[9], AC[10], AC[11], AC[12], AC[13], AC[14], AC[15]);
  and and_1 (p, D7, IR[15], T3);
  not not_1 (not_1_out, IR[15]);
  Decoder3to8 decoder3to8_1 (
    .I0(IR[12]), .I1(IR[13]), .I2(IR[14]), .O0(D0), .O1(D1), .O2(D2), .O3(D3), .out_8(D4), .out_9(D5),
    .out_10(D6), .out_11(D7));
  and and_2 (r_t, D7, not_1_out, T3);
  and and_3 (and_3_out, D4, T4);
  and and_4 (and_4_out, D5, T5);
  or or_2 (LD, and_3_out, and_4_out);
  and and_5 (CLR, R, T1);
  not not_2 (not_2_out, AC[15]);
  not not_3 (not_3_out, AC_t);
  not not_4 (not_4_out, E);
  not not_5 (not_5_out, R);
  and and_6 (and_6_out, D6, T6);
  and and_7 (and_7_out, r_t, not_2_out, IR[4]);
  and and_8 (and_8_out, r_t, AC[15], IR[3]);
  and and_9 (and_9_out, r_t, not_3_out, IR[2]);
  and and_10 (and_10_out, r_t, not_4_out, IR[1]);
  and and_11 (and_11_out, p, FGI, IR[9]);
  and and_12 (and_12_out, p, FGO, IR[8]);
  and and_13 (and_13_out, not_5_out, T1);
  and and_14 (and_14_out, R, T2);
  or or_3 (INC, and_13_out, and_14_out, and_6_out, and_7_out, and_8_out, and_9_out, and_10_out, and_11_out, and_12_out);

  // Other names for the same wires on the sheet: B0 = IR[0]; B1 = IR[1]; B2 = IR[2]; B3 = IR[3]; B4 = IR[4];
  //   B5 = IR[5]; B6 = IR[6]; B7 = IR[7]; B8 = IR[8]; B9 = IR[9]; B10 = IR[10]; B11 = IR[11]; I = IR[15]
endmodule

module DR_controller (
  input  [15:0] IR,
  input  [3:0] COUNTER,
  output LD,
  output INR
);

  wire and_3_out, and_4_out, and_5_out, and_6_out, D0, D1, D2, D3, D4, D5, D6, D7, not_1_out, p, r, T0, T1,
       T2, T3, T4, T5, T6, T7, T8, T9, T10, T11, T12, T13, T14, T15;

  Decoder4to16 decoder4to16_1 (
    .I0(COUNTER[0]), .I1(COUNTER[1]), .I2(COUNTER[2]), .I3(COUNTER[3]), .O1(T0), .O2(T1), .O3(T2), .O4(T3),
    .O5(T4), .O6(T5), .O7(T6), .O8(T7), .O9(T8), .O10(T9), .O11(T10), .O12(T11), .O13(T12), .O14(T13),
    .O15(T14), .O16(T15));
  and and_1 (p, D7, IR[15], T3);
  not not_1 (not_1_out, IR[15]);
  Decoder3to8 decoder3to8_1 (
    .I0(IR[12]), .I1(IR[13]), .I2(IR[14]), .O0(D0), .O1(D1), .O2(D2), .O3(D3), .out_8(D4), .out_9(D5),
    .out_10(D6), .out_11(D7));
  and and_2 (r, D7, not_1_out, T3);
  and and_3 (and_3_out, D0, T4);
  and and_4 (and_4_out, T4, D1);
  and and_5 (and_5_out, T4, D2);
  and and_6 (and_6_out, T4, D6);
  or or_1 (LD, and_3_out, and_4_out, and_5_out, and_6_out);
  and and_7 (INR, D6, T5);

  // Other names for the same wires on the sheet: B0 = IR[0]; B1 = IR[1]; B2 = IR[2]; B3 = IR[3]; B4 = IR[4];
  //   B5 = IR[5]; B6 = IR[6]; B7 = IR[7]; B8 = IR[8]; B9 = IR[9]; B10 = IR[10]; B11 = IR[11]; I = IR[15]
endmodule

module AC_controller (
  input  [15:0] IR,
  input  [3:0] COUNTER,
  output ANDi,
  output ADD,
  output DR,
  output INR,
  output INPR,
  output LD,
  output CLR,
  output COMP,
  output SHR,
  output SHL
);

  wire D0, D1, D2, D3, D4, D5, D6, D7, not_1_out, p, r, T0, T1, T2, T3, T4, T5, T6, T7, T8, T9, T10, T11,
       T12, T13, T14, T15;

  Decoder4to16 decoder4to16_1 (
    .I0(COUNTER[0]), .I1(COUNTER[1]), .I2(COUNTER[2]), .I3(COUNTER[3]), .O1(T0), .O2(T1), .O3(T2), .O4(T3),
    .O5(T4), .O6(T5), .O7(T6), .O8(T7), .O9(T8), .O10(T9), .O11(T10), .O12(T11), .O13(T12), .O14(T13),
    .O15(T14), .O16(T15));
  and and_1 (p, D7, IR[15], T3);
  not not_1 (not_1_out, IR[15]);
  Decoder3to8 decoder3to8_1 (
    .I0(IR[12]), .I1(IR[13]), .I2(IR[14]), .O0(D0), .O1(D1), .O2(D2), .O3(D3), .out_8(D4), .out_9(D5),
    .out_10(D6), .out_11(D7));
  and and_2 (r, D7, not_1_out, T3);
  and and_3 (INR, r, IR[5]);
  and and_4 (CLR, r, IR[11]);
  and and_5 (ANDi, D0, T5);
  and and_6 (ADD, T5, D1);
  and and_7 (DR, D2, T5);
  and and_8 (INPR, p, IR[11]);
  and and_9 (COMP, r, IR[9]);
  and and_10 (SHR, r, IR[7]);
  and and_11 (SHL, r, IR[6]);
  or or_1 (LD, ANDi, ADD, DR, INPR, COMP, SHR, SHL);

  // Other names for the same wires on the sheet: B0 = IR[0]; B1 = IR[1]; B2 = IR[2]; B3 = IR[3]; B4 = IR[4];
  //   B5 = IR[5]; B6 = IR[6]; B7 = IR[7]; B8 = IR[8]; B9 = IR[9]; B10 = IR[10]; B11 = IR[11]; I = IR[15]
endmodule

module IR_controller (
  input  R,
  input  [3:0] COUNTER,
  output LD
);

  wire not_1_out, T0, T1, T2, T3, T4, T5, T6, T7, T8, T9, T10, T11, T12, T13, T14, T15;

  Decoder4to16 decoder4to16_1 (
    .I0(COUNTER[0]), .I1(COUNTER[1]), .I2(COUNTER[2]), .I3(COUNTER[3]), .O1(T0), .O2(T1), .O3(T2), .O4(T3),
    .O5(T4), .O6(T5), .O7(T6), .O8(T7), .O9(T8), .O10(T9), .O11(T10), .O12(T11), .O13(T12), .O14(T13),
    .O15(T14), .O16(T15));
  not not_1 (not_1_out, R);
  and and_1 (LD, not_1_out, T1);
endmodule

module TR_controller (
  input  R,
  input  [3:0] COUNTER,
  output LD
);

  wire not_1_out, T0, T1, T2, T3, T4, T5, T6, T7, T8, T9, T10, T11, T12, T13, T14, T15;

  Decoder4to16 decoder4to16_1 (
    .I0(COUNTER[0]), .I1(COUNTER[1]), .I2(COUNTER[2]), .I3(COUNTER[3]), .O1(T0), .O2(T1), .O3(T2), .O4(T3),
    .O5(T4), .O6(T5), .O7(T6), .O8(T7), .O9(T8), .O10(T9), .O11(T10), .O12(T11), .O13(T12), .O14(T13),
    .O15(T14), .O16(T15));
  not not_1 (not_1_out, R);
  and and_1 (LD, not_1_out, T0);
endmodule

module FlipFlop_controller (
  input  IEN,
  input  FGI,
  input  FGO,
  input  R,
  input  E,
  input  [15:0] IR,
  input  [3:0] COUNTER,
  input  [15:0] AC,
  output SC_set,
  output IEN_reset,
  output S_reset,
  output IEN_set,
  output I_LOAD,
  output R_reset,
  output R_set,
  output FGI_reset,
  output FGO_reset,
  output E_set,
  output E_reset
);

  wire and_3_out, and_4_out, and_5_out, and_6_out, and_7_out, and_8_out, and_9_out, and_10_out, and_11_out,
       and_12_out, and_13_out, and_14_out, and_15_out, and_16_out, and_17_out, and_18_out, and_19_out,
       and_20_out, and_23_out, and_24_out, D0, D1, D2, D3, D4, D5, D6, D7, not_1_out, not_2_out, not_3_out,
       not_4_out, not_5_out, not_6_out, not_7_out, not_8_out, or_5_out, p, r_t, T0, T1, T2, T3, T4, T5, T6,
       T7, T8, T9, T10, T11, T12, T13, T14, T15;

  Decoder4to16 decoder4to16_1 (
    .I0(COUNTER[0]), .I1(COUNTER[1]), .I2(COUNTER[2]), .I3(COUNTER[3]), .O1(T0), .O2(T1), .O3(T2), .O4(T3),
    .O5(T4), .O6(T5), .O7(T6), .O8(T7), .O9(T8), .O10(T9), .O11(T10), .O12(T11), .O13(T12), .O14(T13),
    .O15(T14), .O16(T15));
  and and_1 (p, D7, IR[15], T3);
  not not_1 (not_1_out, IR[15]);
  Decoder3to8 decoder3to8_1 (
    .I0(IR[12]), .I1(IR[13]), .I2(IR[14]), .O0(D0), .O1(D1), .O2(D2), .O3(D3), .out_8(D4), .out_9(D5),
    .out_10(D6), .out_11(D7));
  and and_2 (r_t, D7, not_1_out, T3);
  and and_3 (and_3_out, R, T2);
  and and_4 (and_4_out, D0, T5);
  and and_5 (and_5_out, D1, T5);
  and and_6 (and_6_out, D2, T5);
  and and_7 (and_7_out, D3, T4);
  and and_8 (and_8_out, D4, T4);
  and and_9 (and_9_out, D5, T5);
  and and_10 (and_10_out, D6, T6);
  or or_1 (SC_set, and_3_out, and_4_out, and_5_out, and_6_out, and_7_out, and_8_out, and_9_out, and_10_out, r_t, p);
  not not_2 (not_2_out, E);
  not not_3 (not_3_out, AC[15]);
  not not_4 (not_4_out, R);
  and and_11 (and_11_out, r_t, not_2_out, IR[8]);
  and and_12 (and_12_out, D1, T5, E);
  and and_13 (and_13_out, r_t, AC[15], IR[6]);
  and and_14 (and_14_out, r_t, E, IR[8]);
  and and_15 (and_15_out, D1, T5, E);
  and and_16 (and_16_out, r_t, not_3_out, IR[6]);
  not not_5 (not_5_out, AC[0]);
  and and_17 (and_17_out, not_4_out, T2);
  and and_18 (and_18_out, r_t, AC[0], IR[7]);
  and and_19 (and_19_out, r_t, not_5_out, IR[7]);
  and and_20 (and_20_out, r_t, IR[10]);
  and and_21 (S_reset, r_t, IR[0]);
  and and_22 (I_LOAD, and_17_out, IR[15]);
  or or_2 (E_reset, and_14_out, and_15_out, and_20_out, and_16_out, and_19_out);
  and and_23 (and_23_out, R, T2);
  and and_24 (and_24_out, p, IR[6]);
  or or_3 (E_set, and_11_out, and_12_out, and_13_out, and_18_out);
  or or_4 (IEN_reset, and_23_out, and_24_out);
  and and_25 (IEN_set, p, IR[7]);
  and and_26 (R_reset, r_t, T2);
  and and_27 (FGI_reset, p, IR[11]);
  and and_28 (FGO_reset, p, IR[10]);
  or or_5 (or_5_out, FGI, FGO);
  not not_6 (not_6_out, T0);
  not not_7 (not_7_out, T1);
  and and_29 (R_set, or_5_out, IEN, not_6_out, not_7_out, not_8_out);
  not not_8 (not_8_out, T2);

  // Other names for the same wires on the sheet: B0 = IR[0]; B1 = IR[1]; B2 = IR[2]; B3 = IR[3]; B4 = IR[4];
  //   B5 = IR[5]; B6 = IR[6]; B7 = IR[7]; B8 = IR[8]; B9 = IR[9]; B10 = IR[10]; B11 = IR[11]; AC_0 = AC[0];
  //   AC_1 = AC[1]; AC_2 = AC[2]; AC_3 = AC[3]; AC_4 = AC[4]; AC_5 = AC[5]; AC_6 = AC[6]; AC_7 = AC[7]; AC_8 = AC[8];
  //   AC_9 = AC[9]; AC_10 = AC[10]; AC_11 = AC[11]; AC_12 = AC[12]; AC_13 = AC[13]; AC_14 = AC[14]; AC_15 = AC[15];
  //   I = IR[15]
endmodule

module OUTR_controller (
  input  [15:0] IR,
  input  [3:0] COUNTER,
  output LD
);

  wire D0, D1, D2, D3, D4, D5, D6, D7, p, T0, T1, T2, T3, T4, T5, T6, T7, T8, T9, T10, T11, T12, T13, T14,
       T15;

  Decoder4to16 decoder4to16_1 (
    .I0(COUNTER[0]), .I1(COUNTER[1]), .I2(COUNTER[2]), .I3(COUNTER[3]), .O1(T0), .O2(T1), .O3(T2), .O4(T3),
    .O5(T4), .O6(T5), .O7(T6), .O8(T7), .O9(T8), .O10(T9), .O11(T10), .O12(T11), .O13(T12), .O14(T13),
    .O15(T14), .O16(T15));
  and and_1 (p, D7, IR[15], T3);
  and and_2 (LD, p, IR[10]);
  Decoder3to8 decoder3to8_1 (
    .I0(IR[12]), .I1(IR[13]), .I2(IR[14]), .O0(D0), .O1(D1), .O2(D2), .O3(D3), .out_8(D4), .out_9(D5),
    .out_10(D6), .out_11(D7));

  // Other names for the same wires on the sheet: B0 = IR[0]; B1 = IR[1]; B2 = IR[2]; B3 = IR[3]; B4 = IR[4];
  //   B5 = IR[5]; B6 = IR[6]; B7 = IR[7]; B8 = IR[8]; B9 = IR[9]; B10 = IR[10]; B11 = IR[11]; I = IR[15]
endmodule

module ALU_1 (
  input  [6:0] control,
  input  AC_i,
  input  DR_i,
  input  Carry_in,
  input  INPR_i,
  input  AC_forward,
  input  AC_backwards,
  output Carry_out,
  output AC
);

  wire ADD_out, adder1bit_1_sum, ANDi_out, COMP_out, DR_out, INPR_out, not_1_out, SHL_out, SHR_out;

  Adder1bit adder1bit_1 (.A(AC_i), .B(DR_i), .Cin(Carry_in), .Sum(adder1bit_1_sum), .Carry(Carry_out));
  not not_1 (not_1_out, AC_i);
  and ANDi (ANDi_out, control[0], AC_i, DR_i);
  and ADD (ADD_out, control[1], adder1bit_1_sum);
  and DR (DR_out, control[2], DR_i);
  and INPR (INPR_out, control[3], INPR_i);
  and COMP (COMP_out, control[4], not_1_out);
  and SHR (SHR_out, control[5], AC_forward);
  and SHL (SHL_out, control[6], AC_backwards);
  or or_1 (AC, ANDi_out, ADD_out, DR_out, INPR_out, COMP_out, SHR_out, SHL_out);
endmodule

module ALU_16 (
  input  [15:0] AC,
  input  [15:0] DR,
  input  [7:0] INPR,
  input  ANDi,
  input  ADD,
  input  DRi,
  input  INPRi,
  input  COMP,
  input  SHR,
  input  SHL,
  input  E_IN,
  output [15:0] OUPT,
  output E_out
);

  wire AC_16, alu_1_1_carry_out, alu_1_2_carry_out, alu_1_3_carry_out, alu_1_4_carry_out, alu_1_5_carry_out,
       alu_1_6_carry_out, alu_1_7_carry_out, alu_1_8_carry_out, alu_1_9_carry_out, alu_1_10_carry_out,
       alu_1_11_carry_out, alu_1_12_carry_out, alu_1_13_carry_out, alu_1_14_carry_out, alu_1_15_carry_out,
       and_1_out, and_2_out, and_3_out, and_4_out, nor_1_out;

  and and_1 (and_1_out, AC[15], SHL);
  and and_2 (and_2_out, AC[0], SHR);
  and and_3 (and_3_out, ADD, AC_16);
  nor nor_1 (nor_1_out, SHR, SHL, ADD);
  and and_4 (and_4_out, nor_1_out, E_IN);
  or or_1 (E_out, and_1_out, and_2_out, and_3_out, and_4_out);
  ALU_1 alu_1_1 (
    .Carry_in(1'b0), .AC_forward(AC[1]), .AC_backwards(E_IN), .INPR_i(INPR[0]),
    .control({SHL, SHR, COMP, INPRi, DRi, ADD, ANDi}), .DR_i(DR[0]), .AC_i(AC[0]),
    .Carry_out(alu_1_1_carry_out), .AC(OUPT[0]));
  ALU_1 alu_1_2 (
    .Carry_in(alu_1_1_carry_out), .AC_forward(AC[2]), .AC_backwards(AC[0]), .INPR_i(INPR[1]),
    .control({SHL, SHR, COMP, INPRi, DRi, ADD, ANDi}), .DR_i(DR[1]), .AC_i(AC[1]),
    .Carry_out(alu_1_2_carry_out), .AC(OUPT[1]));
  ALU_1 alu_1_3 (
    .Carry_in(alu_1_2_carry_out), .AC_forward(AC[3]), .AC_backwards(AC[1]), .INPR_i(INPR[2]),
    .control({SHL, SHR, COMP, INPRi, DRi, ADD, ANDi}), .DR_i(DR[2]), .AC_i(AC[2]),
    .Carry_out(alu_1_3_carry_out), .AC(OUPT[2]));
  ALU_1 alu_1_4 (
    .Carry_in(alu_1_3_carry_out), .AC_forward(AC[4]), .AC_backwards(AC[2]), .INPR_i(INPR[3]),
    .control({SHL, SHR, COMP, INPRi, DRi, ADD, ANDi}), .DR_i(DR[3]), .AC_i(AC[3]),
    .Carry_out(alu_1_4_carry_out), .AC(OUPT[3]));
  ALU_1 alu_1_5 (
    .Carry_in(alu_1_4_carry_out), .AC_forward(AC[5]), .AC_backwards(AC[3]), .INPR_i(INPR[4]),
    .control({SHL, SHR, COMP, INPRi, DRi, ADD, ANDi}), .DR_i(DR[4]), .AC_i(AC[4]),
    .Carry_out(alu_1_5_carry_out), .AC(OUPT[4]));
  ALU_1 alu_1_6 (
    .Carry_in(alu_1_5_carry_out), .AC_forward(AC[6]), .AC_backwards(AC[4]), .INPR_i(INPR[5]),
    .control({SHL, SHR, COMP, INPRi, DRi, ADD, ANDi}), .DR_i(DR[5]), .AC_i(AC[5]),
    .Carry_out(alu_1_6_carry_out), .AC(OUPT[5]));
  ALU_1 alu_1_7 (
    .Carry_in(alu_1_6_carry_out), .AC_forward(AC[7]), .AC_backwards(AC[5]), .INPR_i(INPR[6]),
    .control({SHL, SHR, COMP, INPRi, DRi, ADD, ANDi}), .DR_i(DR[6]), .AC_i(AC[6]),
    .Carry_out(alu_1_7_carry_out), .AC(OUPT[6]));
  ALU_1 alu_1_8 (
    .Carry_in(alu_1_7_carry_out), .AC_forward(AC[8]), .AC_backwards(AC[6]), .INPR_i(INPR[7]),
    .control({SHL, SHR, COMP, INPRi, DRi, ADD, ANDi}), .DR_i(DR[7]), .AC_i(AC[7]),
    .Carry_out(alu_1_8_carry_out), .AC(OUPT[7]));
  ALU_1 alu_1_9 (
    .Carry_in(alu_1_8_carry_out), .AC_forward(AC[9]), .AC_backwards(AC[7]), .INPR_i(1'b0),
    .control({SHL, SHR, COMP, INPRi, DRi, ADD, ANDi}), .DR_i(DR[8]), .AC_i(AC[8]),
    .Carry_out(alu_1_9_carry_out), .AC(OUPT[8]));
  ALU_1 alu_1_10 (
    .Carry_in(alu_1_9_carry_out), .AC_forward(AC[10]), .AC_backwards(AC[8]), .INPR_i(1'b0),
    .control({SHL, SHR, COMP, INPRi, DRi, ADD, ANDi}), .DR_i(DR[9]), .AC_i(AC[9]),
    .Carry_out(alu_1_10_carry_out), .AC(OUPT[9]));
  ALU_1 alu_1_11 (
    .Carry_in(alu_1_10_carry_out), .AC_forward(AC[11]), .AC_backwards(AC[9]), .INPR_i(1'b0),
    .control({SHL, SHR, COMP, INPRi, DRi, ADD, ANDi}), .DR_i(DR[10]), .AC_i(AC[10]),
    .Carry_out(alu_1_11_carry_out), .AC(OUPT[10]));
  ALU_1 alu_1_12 (
    .Carry_in(alu_1_11_carry_out), .AC_forward(AC[12]), .AC_backwards(AC[10]), .INPR_i(1'b0),
    .control({SHL, SHR, COMP, INPRi, DRi, ADD, ANDi}), .DR_i(DR[11]), .AC_i(AC[11]),
    .Carry_out(alu_1_12_carry_out), .AC(OUPT[11]));
  ALU_1 alu_1_13 (
    .Carry_in(alu_1_12_carry_out), .AC_forward(AC[13]), .AC_backwards(AC[11]), .INPR_i(1'b0),
    .control({SHL, SHR, COMP, INPRi, DRi, ADD, ANDi}), .DR_i(DR[12]), .AC_i(AC[12]),
    .Carry_out(alu_1_13_carry_out), .AC(OUPT[12]));
  ALU_1 alu_1_14 (
    .Carry_in(alu_1_13_carry_out), .AC_forward(AC[14]), .AC_backwards(AC[12]), .INPR_i(1'b0),
    .control({SHL, SHR, COMP, INPRi, DRi, ADD, ANDi}), .DR_i(DR[13]), .AC_i(AC[13]),
    .Carry_out(alu_1_14_carry_out), .AC(OUPT[13]));
  ALU_1 alu_1_15 (
    .Carry_in(alu_1_14_carry_out), .AC_forward(AC[15]), .AC_backwards(AC[13]), .INPR_i(1'b0),
    .control({SHL, SHR, COMP, INPRi, DRi, ADD, ANDi}), .DR_i(DR[14]), .AC_i(AC[14]),
    .Carry_out(alu_1_15_carry_out), .AC(OUPT[14]));
  ALU_1 alu_1_16 (
    .Carry_in(alu_1_15_carry_out), .AC_forward(E_IN), .AC_backwards(AC[14]), .INPR_i(1'b0),
    .control({SHL, SHR, COMP, INPRi, DRi, ADD, ANDi}), .DR_i(DR[15]), .AC_i(AC[15]), .Carry_out(AC_16),
    .AC(OUPT[15]));

  // Other names for the same wires on the sheet: AC_0 = AC[0]; AC_1 = AC[1]; AC_2 = AC[2]; AC_3 = AC[3]; AC_4 = AC[4];
  //   AC_5 = AC[5]; AC_6 = AC[6]; AC_7 = AC[7]; AC_8 = AC[8]; AC_9 = AC[9]; AC_10 = AC[10]; AC_11 = AC[11];
  //   AC_12 = AC[12]; AC_13 = AC[13]; AC_14 = AC[14]; AC_15 = AC[15];
  //   CNTRL[6:0] = {SHL, SHR, COMP, INPRi, DRi, ADD, ANDi}; DR_t = DRi; INPR_t = INPRi; DR_0 = DR[0]; DR_1 = DR[1];
  //   DR_2 = DR[2]; DR_3 = DR[3]; DR_4 = DR[4]; DR_5 = DR[5]; DR_6 = DR[6]; DR_7 = DR[7]; DR_8 = DR[8]; DR_9 = DR[9];
  //   DR_10 = DR[10]; DR_11 = DR[11]; DR_12 = DR[12]; DR_13 = DR[13]; DR_14 = DR[14]; DR_15 = DR[15];
  //   INPR_0 = INPR[0]; INPR_1 = INPR[1]; INPR_2 = INPR[2]; INPR_3 = INPR[3]; INPR_4 = INPR[4]; INPR_5 = INPR[5];
  //   INPR_6 = INPR[6]; INPR_7 = INPR[7]
endmodule

module mem16 (
  input  [11:0] Address,
  input  reset,
  input  load,
  input  [15:0] I,
  input  CLK,
  output [15:0] out_6
);

  wire A0, A1, A2, A3, A4, A5, A6, A7, A8, A9, A10, A11, A12, A13, A14, A15, A16, A17, A18, A19, A20, A21,
       A22, A23, A24, A25, A26, A27, A28, A29, A30, A31, and_1_out, and_2_out, and_3_out, and_4_out,
       and_5_out, and_6_out, and_7_out, and_8_out, and_9_out, and_10_out, and_11_out, and_12_out, and_13_out,
       and_14_out, and_15_out, and_16_out, and_17_out, and_18_out, and_19_out, and_20_out, and_21_out,
       and_22_out, and_23_out, and_24_out, and_25_out, and_26_out, and_27_out, and_28_out, and_29_out,
       and_30_out, and_31_out, and_32_out;
  wire [15:0] mux_r16_1_o, mux_r16_2_o, mux_r16_3_o, mux_r16_4_o, mux_r16_5_o, mux_r16_6_o, mux_r16_7_o,
       mux_r16_8_o, mux_r16_9_o, mux_r16_10_o, mux_r16_11_o, mux_r16_12_o, mux_r16_13_o, mux_r16_14_o,
       mux_r16_15_o, mux_r16_16_o, mux_r16_17_o, mux_r16_18_o, mux_r16_19_o, mux_r16_20_o, mux_r16_21_o,
       mux_r16_22_o, mux_r16_23_o, mux_r16_24_o, mux_r16_25_o, mux_r16_26_o, mux_r16_27_o, mux_r16_28_o,
       mux_r16_29_o, mux_r16_30_o, mux_r16_31_o, mux_r16_32_o, O0, O1, O2, O3, O4, O5, O6, O7, O8, O9, O10,
       O11, O12, O13, O14, O15, O16, O17, O18, O19, O20, O21, O22, O23, O24, O25, O26, O27, O28, O29, O30,
       O31;

  Decoder5to32 decoder5to32_1 (
    .I0(Address[0]), .I1(Address[1]), .I2(Address[2]), .I3(Address[3]), .I5(Address[4]), .O1(A0), .O2(A1),
    .O3(A2), .O4(A3), .O5(A4), .O6(A5), .O7(A6), .O8(A7), .O9(A8), .O10(A9), .O11(A10), .O12(A11), .O13(A12),
    .O14(A13), .O15(A14), .O16(A15), .O17(A16), .O18(A17), .O19(A18), .O20(A19), .O21(A20), .O22(A21),
    .O23(A22), .O24(A23), .O25(A24), .O26(A25), .O27(A26), .O28(A27), .O29(A28), .O30(A29), .O31(A30),
    .O32(A31));
  and and_1 (and_1_out, load, A0);
  and and_2 (and_2_out, load, A1);
  and and_3 (and_3_out, load, A2);
  and and_4 (and_4_out, load, A3);
  and and_5 (and_5_out, load, A4);
  and and_6 (and_6_out, load, A5);
  and and_7 (and_7_out, load, A6);
  and and_8 (and_8_out, load, A7);
  and and_9 (and_9_out, load, A8);
  and and_10 (and_10_out, load, A9);
  and and_11 (and_11_out, load, A10);
  and and_12 (and_12_out, load, A11);
  and and_13 (and_13_out, load, A12);
  and and_14 (and_14_out, load, A13);
  and and_15 (and_15_out, load, A14);
  and and_16 (and_16_out, load, A15);
  and and_17 (and_17_out, load, A16);
  and and_18 (and_18_out, load, A17);
  and and_19 (and_19_out, load, A18);
  and and_20 (and_20_out, load, A19);
  and and_21 (and_21_out, load, A20);
  and and_22 (and_22_out, load, A21);
  and and_23 (and_23_out, load, A22);
  and and_24 (and_24_out, load, A23);
  and and_25 (and_25_out, load, A24);
  and and_26 (and_26_out, load, A25);
  and and_27 (and_27_out, load, A26);
  and and_28 (and_28_out, load, A27);
  and and_29 (and_29_out, load, A28);
  and and_30 (and_30_out, load, A29);
  and and_31 (and_31_out, load, A30);
  and and_32 (and_32_out, load, A31);
  mux_r16 mux_r16_1 (.A(and_1_out), .I1(O0), .I2(I), .O(mux_r16_1_o));
  mux_r16 mux_r16_2 (.A(and_2_out), .I1(O1), .I2(I), .O(mux_r16_2_o));
  mux_r16 mux_r16_3 (.A(and_3_out), .I1(O2), .I2(I), .O(mux_r16_3_o));
  mux_r16 mux_r16_4 (.A(and_4_out), .I1(O3), .I2(I), .O(mux_r16_4_o));
  mux_r16 mux_r16_5 (.A(and_5_out), .I1(O4), .I2(I), .O(mux_r16_5_o));
  mux_r16 mux_r16_6 (.A(and_6_out), .I1(O5), .I2(I), .O(mux_r16_6_o));
  mux_r16 mux_r16_7 (.A(and_7_out), .I1(O6), .I2(I), .O(mux_r16_7_o));
  mux_r16 mux_r16_8 (.A(and_8_out), .I1(O7), .I2(I), .O(mux_r16_8_o));
  mux_r16 mux_r16_9 (.A(and_9_out), .I1(O8), .I2(I), .O(mux_r16_9_o));
  mux_r16 mux_r16_10 (.A(and_10_out), .I1(O9), .I2(I), .O(mux_r16_10_o));
  mux_r16 mux_r16_11 (.A(and_11_out), .I1(O10), .I2(I), .O(mux_r16_11_o));
  mux_r16 mux_r16_12 (.A(and_12_out), .I1(O11), .I2(I), .O(mux_r16_12_o));
  mux_r16 mux_r16_13 (.A(and_13_out), .I1(O12), .I2(I), .O(mux_r16_13_o));
  mux_r16 mux_r16_14 (.A(and_14_out), .I1(O13), .I2(I), .O(mux_r16_14_o));
  mux_r16 mux_r16_15 (.A(and_15_out), .I1(O14), .I2(I), .O(mux_r16_15_o));
  mux_r16 mux_r16_16 (.A(and_16_out), .I1(O15), .I2(I), .O(mux_r16_16_o));
  mux_r16 mux_r16_17 (.A(and_17_out), .I1(O16), .I2(I), .O(mux_r16_17_o));
  mux_r16 mux_r16_18 (.A(and_18_out), .I1(O17), .I2(I), .O(mux_r16_18_o));
  mux_r16 mux_r16_19 (.A(and_19_out), .I1(O18), .I2(I), .O(mux_r16_19_o));
  mux_r16 mux_r16_20 (.A(and_20_out), .I1(O19), .I2(I), .O(mux_r16_20_o));
  mux_r16 mux_r16_21 (.A(and_21_out), .I1(O20), .I2(I), .O(mux_r16_21_o));
  mux_r16 mux_r16_22 (.A(and_22_out), .I1(O21), .I2(I), .O(mux_r16_22_o));
  mux_r16 mux_r16_23 (.A(and_23_out), .I1(O22), .I2(I), .O(mux_r16_23_o));
  mux_r16 mux_r16_24 (.A(and_24_out), .I1(O23), .I2(I), .O(mux_r16_24_o));
  mux_r16 mux_r16_25 (.A(and_25_out), .I1(O24), .I2(I), .O(mux_r16_25_o));
  mux_r16 mux_r16_26 (.A(and_26_out), .I1(O25), .I2(I), .O(mux_r16_26_o));
  mux_r16 mux_r16_27 (.A(and_27_out), .I1(O26), .I2(I), .O(mux_r16_27_o));
  mux_r16 mux_r16_28 (.A(and_28_out), .I1(O27), .I2(I), .O(mux_r16_28_o));
  mux_r16 mux_r16_29 (.A(and_29_out), .I1(O28), .I2(I), .O(mux_r16_29_o));
  mux_r16 mux_r16_30 (.A(and_30_out), .I1(O29), .I2(I), .O(mux_r16_30_o));
  mux_r16 mux_r16_31 (.A(and_31_out), .I1(O30), .I2(I), .O(mux_r16_31_o));
  mux_r16 mux_r16_32 (.A(and_32_out), .I1(O31), .I2(I), .O(mux_r16_32_o));
  MUX32TO1 mux32to1_1 (
    .S4(Address[4]), .S3(Address[3]), .in_32(O26), .in_33(O27), .in_34(O28), .in_35(O29), .in_36(O30),
    .I31(O31), .I0(O0), .in_7(O1), .in_8(O2), .in_9(O3), .in_10(O4), .in_11(O5), .in_12(O6), .in_13(O7),
    .in_14(O8), .in_15(O9), .in_16(O10), .in_17(O11), .in_18(O12), .in_19(O13), .in_20(O14), .in_21(O15),
    .in_22(O16), .in_23(O17), .in_24(O18), .in_25(O19), .in_26(O20), .in_27(O21), .in_28(O22), .in_29(O23),
    .in_30(O24), .in_31(O25), .S2(Address[2]), .S1(Address[1]), .SO(Address[0]), .O(out_6));
  Reg16bit reg16bit_1 (.reset(reset), .clk(CLK), .I(mux_r16_1_o), .out_5(O0));  // open: set
  Reg16bit reg16bit_2 (.reset(reset), .clk(CLK), .I(mux_r16_2_o), .out_5(O1));  // open: set
  Reg16bit reg16bit_3 (.reset(reset), .clk(CLK), .I(mux_r16_3_o), .out_5(O2));  // open: set
  Reg16bit reg16bit_4 (.reset(reset), .clk(CLK), .I(mux_r16_4_o), .out_5(O3));  // open: set
  Reg16bit reg16bit_5 (.reset(reset), .clk(CLK), .I(mux_r16_5_o), .out_5(O4));  // open: set
  Reg16bit reg16bit_6 (.reset(reset), .clk(CLK), .I(mux_r16_6_o), .out_5(O5));  // open: set
  Reg16bit reg16bit_7 (.reset(reset), .clk(CLK), .I(mux_r16_7_o), .out_5(O6));  // open: set
  Reg16bit reg16bit_8 (.reset(reset), .clk(CLK), .I(mux_r16_8_o), .out_5(O7));  // open: set
  Reg16bit reg16bit_9 (.reset(reset), .clk(CLK), .I(mux_r16_9_o), .out_5(O8));  // open: set
  Reg16bit reg16bit_10 (.reset(reset), .clk(CLK), .I(mux_r16_10_o), .out_5(O9));  // open: set
  Reg16bit reg16bit_11 (.reset(reset), .clk(CLK), .I(mux_r16_11_o), .out_5(O10));  // open: set
  Reg16bit reg16bit_12 (.reset(reset), .clk(CLK), .I(mux_r16_12_o), .out_5(O11));  // open: set
  Reg16bit reg16bit_13 (.reset(reset), .clk(CLK), .I(mux_r16_13_o), .out_5(O12));  // open: set
  Reg16bit reg16bit_14 (.reset(reset), .clk(CLK), .I(mux_r16_14_o), .out_5(O13));  // open: set
  Reg16bit reg16bit_15 (.reset(reset), .clk(CLK), .I(mux_r16_15_o), .out_5(O14));  // open: set
  Reg16bit reg16bit_16 (.reset(reset), .clk(CLK), .I(mux_r16_16_o), .out_5(O15));  // open: set
  Reg16bit reg16bit_17 (.reset(reset), .clk(CLK), .I(mux_r16_17_o), .out_5(O16));  // open: set
  Reg16bit reg16bit_18 (.reset(reset), .clk(CLK), .I(mux_r16_18_o), .out_5(O17));  // open: set
  Reg16bit reg16bit_19 (.reset(reset), .clk(CLK), .I(mux_r16_19_o), .out_5(O18));  // open: set
  Reg16bit reg16bit_20 (.reset(reset), .clk(CLK), .I(mux_r16_20_o), .out_5(O19));  // open: set
  Reg16bit reg16bit_21 (.reset(reset), .clk(CLK), .I(mux_r16_21_o), .out_5(O20));  // open: set
  Reg16bit reg16bit_22 (.reset(reset), .clk(CLK), .I(mux_r16_22_o), .out_5(O21));  // open: set
  Reg16bit reg16bit_23 (.reset(reset), .clk(CLK), .I(mux_r16_23_o), .out_5(O22));  // open: set
  Reg16bit reg16bit_24 (.reset(reset), .clk(CLK), .I(mux_r16_24_o), .out_5(O23));  // open: set
  Reg16bit reg16bit_25 (.reset(reset), .clk(CLK), .I(mux_r16_25_o), .out_5(O24));  // open: set
  Reg16bit reg16bit_26 (.reset(reset), .clk(CLK), .I(mux_r16_26_o), .out_5(O25));  // open: set
  Reg16bit reg16bit_27 (.reset(reset), .clk(CLK), .I(mux_r16_27_o), .out_5(O26));  // open: set
  Reg16bit reg16bit_28 (.reset(reset), .clk(CLK), .I(mux_r16_28_o), .out_5(O27));  // open: set
  Reg16bit reg16bit_29 (.reset(reset), .clk(CLK), .I(mux_r16_29_o), .out_5(O28));  // open: set
  Reg16bit reg16bit_30 (.reset(reset), .clk(CLK), .I(mux_r16_30_o), .out_5(O29));  // open: set
  Reg16bit reg16bit_31 (.reset(reset), .clk(CLK), .I(mux_r16_31_o), .out_5(O30));  // open: set
  Reg16bit reg16bit_32 (.reset(reset), .clk(CLK), .I(mux_r16_32_o), .out_5(O31));  // open: set

  // Other names for the same wires on the sheet: ADDRESS_t[4:0] = Address[4:0]
endmodule

module mem_controller (
  input  R,
  input  [15:0] IR,
  input  [3:0] COUNTER,
  output WRITE,
  output READ
);

  wire and_3_out, and_4_out, and_5_out, and_6_out, and_7_out, and_8_out, and_9_out, and_10_out, and_11_out,
       and_12_out, D0, D1, D2, D3, D4, D5, D6, D7, not_1_out, not_2_out, not_3_out, p, r_t, T0, T1, T2, T3,
       T4, T5, T6, T7, T8, T9, T10, T11, T12, T13, T14, T15;

  Decoder4to16 decoder4to16_1 (
    .I0(COUNTER[0]), .I1(COUNTER[1]), .I2(COUNTER[2]), .I3(COUNTER[3]), .O1(T0), .O2(T1), .O3(T2), .O4(T3),
    .O5(T4), .O6(T5), .O7(T6), .O8(T7), .O9(T8), .O10(T9), .O11(T10), .O12(T11), .O13(T12), .O14(T13),
    .O15(T14), .O16(T15));
  and and_1 (p, D7, IR[15], T3);
  not not_1 (not_1_out, IR[15]);
  Decoder3to8 decoder3to8_1 (
    .I0(IR[12]), .I1(IR[13]), .I2(IR[14]), .O0(D0), .O1(D1), .O2(D2), .O3(D3), .out_8(D4), .out_9(D5),
    .out_10(D6), .out_11(D7));
  and and_2 (r_t, D7, not_1_out, T3);
  not not_2 (not_2_out, R);
  not not_3 (not_3_out, D7);
  and and_3 (and_3_out, D2, T4);
  and and_4 (and_4_out, not_2_out, T1);
  and and_5 (and_5_out, not_3_out, IR[15], T3);
  and and_6 (and_6_out, D0, T4);
  and and_7 (and_7_out, D1, T4);
  and and_8 (and_8_out, D6, T4);
  or or_1 (READ, and_4_out, and_5_out, and_6_out, and_7_out, and_3_out, and_8_out);
  and and_9 (and_9_out, R, T1);
  and and_10 (and_10_out, D6, T6);
  and and_11 (and_11_out, D3, T4);
  and and_12 (and_12_out, D5, T4);
  or or_2 (WRITE, and_9_out, and_10_out, and_11_out, and_12_out);

  // Other names for the same wires on the sheet: B0 = IR[0]; B1 = IR[1]; B2 = IR[2]; B3 = IR[3]; B4 = IR[4];
  //   B5 = IR[5]; B6 = IR[6]; B7 = IR[7]; B8 = IR[8]; B9 = IR[9]; B10 = IR[10]; B11 = IR[11]; I = IR[15]
endmodule

module Decoder5to32 (
  input  I0,
  input  I1,
  input  I2,
  input  I3,
  input  I5,
  output O1,
  output O2,
  output O3,
  output O4,
  output O5,
  output O6,
  output O7,
  output O8,
  output O9,
  output O10,
  output O11,
  output O12,
  output O13,
  output O14,
  output O15,
  output O16,
  output O17,
  output O18,
  output O19,
  output O20,
  output O21,
  output O22,
  output O23,
  output O24,
  output O25,
  output O26,
  output O27,
  output O28,
  output O29,
  output O30,
  output O31,
  output O32
);

  wire decoder2to4_1_o2, decoder2to4_1_o3, decoder2to4_2_o0, decoder2to4_2_o1, decoder2to4_2_o2,
       decoder2to4_2_o3, decoder2to4_3_o0, decoder2to4_3_o1, decoder2to4_3_o2, decoder2to4_3_o3;

  Decoder2to4 decoder2to4_1 (
    .I1(1'b1), .I0(I5), .enable(1'b1), .O2(decoder2to4_1_o2), .O3(decoder2to4_1_o3));  // open: O0, O1
  Decoder2to4 decoder2to4_2 (
    .I1(I3), .I0(I2), .enable(decoder2to4_1_o2), .O0(decoder2to4_2_o0), .O1(decoder2to4_2_o1),
    .O2(decoder2to4_2_o2), .O3(decoder2to4_2_o3));
  Decoder2to4 decoder2to4_3 (
    .I1(I3), .I0(I2), .enable(decoder2to4_1_o3), .O0(decoder2to4_3_o0), .O1(decoder2to4_3_o1),
    .O2(decoder2to4_3_o2), .O3(decoder2to4_3_o3));
  Decoder2to4 decoder2to4_4 (.I1(I1), .I0(I0), .enable(decoder2to4_2_o0), .O0(O1), .O1(O2), .O2(O3), .O3(O4));
  Decoder2to4 decoder2to4_5 (.I1(I1), .I0(I0), .enable(decoder2to4_2_o1), .O0(O5), .O1(O6), .O2(O7), .O3(O8));
  Decoder2to4 decoder2to4_6 (.I1(I1), .I0(I0), .enable(decoder2to4_2_o2), .O0(O9), .O1(O10), .O2(O11), .O3(O12));
  Decoder2to4 decoder2to4_7 (.I1(I1), .I0(I0), .enable(decoder2to4_2_o3), .O0(O13), .O1(O14), .O2(O15), .O3(O16));
  Decoder2to4 decoder2to4_8 (.I1(I1), .I0(I0), .enable(decoder2to4_3_o0), .O0(O17), .O1(O18), .O2(O19), .O3(O20));
  Decoder2to4 decoder2to4_9 (.I1(I1), .I0(I0), .enable(decoder2to4_3_o1), .O0(O21), .O1(O22), .O2(O23), .O3(O24));
  Decoder2to4 decoder2to4_10 (.I1(I1), .I0(I0), .enable(decoder2to4_3_o2), .O0(O25), .O1(O26), .O2(O27), .O3(O28));
  Decoder2to4 decoder2to4_11 (.I1(I1), .I0(I0), .enable(decoder2to4_3_o3), .O0(O29), .O1(O30), .O2(O31), .O3(O32));
endmodule

module mux8into1 (
  input  S0,
  input  [15:0] I0,
  input  S1,
  input  [15:0] I1,
  input  S2,
  input  [15:0] I2,
  input  [15:0] I3,
  input  [15:0] I4,
  input  [15:0] I5,
  input  [15:0] I6,
  input  [15:0] I7,
  output [15:0] OPT
);

  wire [15:0] mux_r16_1_o, mux_r16_2_o, mux_r16_3_o, mux_r16_4_o, mux_r16_5_o, mux_r16_6_o;

  mux_r16 mux_r16_1 (.A(S0), .I1(I0), .I2(I1), .O(mux_r16_1_o));
  mux_r16 mux_r16_2 (.A(S0), .I1(I2), .I2(I3), .O(mux_r16_2_o));
  mux_r16 mux_r16_3 (.A(S0), .I1(I4), .I2(I5), .O(mux_r16_3_o));
  mux_r16 mux_r16_4 (.A(S0), .I1(I6), .I2(I7), .O(mux_r16_4_o));
  mux_r16 mux_r16_5 (.A(S1), .I1(mux_r16_1_o), .I2(mux_r16_2_o), .O(mux_r16_5_o));
  mux_r16 mux_r16_6 (.A(S1), .I1(mux_r16_3_o), .I2(mux_r16_4_o), .O(mux_r16_6_o));
  mux_r16 mux_r16_7 (.A(S2), .I1(mux_r16_5_o), .I2(mux_r16_6_o), .O(OPT));
endmodule

module MUX32TO1 (
  input  SO,
  input  S1,
  input  S2,
  input  S3,
  input  S4,
  input  [15:0] I0,
  input  [15:0] in_7,
  input  [15:0] in_8,
  input  [15:0] in_9,
  input  [15:0] in_10,
  input  [15:0] in_11,
  input  [15:0] in_12,
  input  [15:0] in_13,
  input  [15:0] in_14,
  input  [15:0] in_15,
  input  [15:0] in_16,
  input  [15:0] in_17,
  input  [15:0] in_18,
  input  [15:0] in_19,
  input  [15:0] in_20,
  input  [15:0] in_21,
  input  [15:0] in_22,
  input  [15:0] in_23,
  input  [15:0] in_24,
  input  [15:0] in_25,
  input  [15:0] in_26,
  input  [15:0] in_27,
  input  [15:0] in_28,
  input  [15:0] in_29,
  input  [15:0] in_30,
  input  [15:0] in_31,
  input  [15:0] in_32,
  input  [15:0] in_33,
  input  [15:0] in_34,
  input  [15:0] in_35,
  input  [15:0] in_36,
  input  [15:0] I31,
  output [15:0] O
);

  wire [15:0] mux8into1_1_opt, mux8into1_2_opt, mux8into1_3_opt, mux8into1_4_opt;

  mux8into1 mux8into1_1 (
    .S0(SO), .I0(I0), .S1(S1), .I1(in_7), .S2(S2), .I2(in_8), .I3(in_9), .I4(in_10), .I5(in_11), .I6(in_12),
    .I7(in_13), .OPT(mux8into1_1_opt));
  mux8into1 mux8into1_2 (
    .S0(SO), .I0(in_14), .S1(S1), .I1(in_15), .S2(S2), .I2(in_16), .I3(in_17), .I4(in_18), .I5(in_19),
    .I6(in_20), .I7(in_21), .OPT(mux8into1_2_opt));
  mux8into1 mux8into1_3 (
    .S0(SO), .I0(in_22), .S1(S1), .I1(in_23), .S2(S2), .I2(in_24), .I3(in_25), .I4(in_26), .I5(in_27),
    .I6(in_28), .I7(in_29), .OPT(mux8into1_3_opt));
  mux8into1 mux8into1_4 (
    .S0(SO), .I0(in_30), .S1(S1), .I1(in_31), .S2(S2), .I2(in_32), .I3(in_33), .I4(in_34), .I5(in_35),
    .I6(in_36), .I7(I31), .OPT(mux8into1_4_opt));
  mux4into1 mux4into1_1 (
    .S0(S3), .S1(S4), .I0(mux8into1_1_opt), .I1(mux8into1_2_opt), .I2(mux8into1_3_opt), .I3(mux8into1_4_opt),
    .OPT(O));
endmodule

module mux4into1 (
  input  S0,
  input  S1,
  input  [15:0] I0,
  input  [15:0] I1,
  input  [15:0] I2,
  input  [15:0] I3,
  output [15:0] OPT
);

  wire [15:0] mux_r16_1_o, mux_r16_2_o;

  mux_r16 mux_r16_1 (.A(S0), .I1(I0), .I2(I1), .O(mux_r16_1_o));
  mux_r16 mux_r16_2 (.A(S0), .I1(I2), .I2(I3), .O(mux_r16_2_o));
  mux_r16 mux_r16_3 (.A(S1), .I1(mux_r16_1_o), .I2(mux_r16_2_o), .O(OPT));
endmodule
